# Fritzing sketch data_logger_oled (saved by Fritzing 0.9.3b)
breadboards: 1

parts:
  Grove1 = Grove OLED 128x96
  Part1 = Arduino Uno (Rev3) - ICSP  # not connected
  Part2 = DHT22 module
  Part3 = Memoire 1.0 - SD card log shield

nets:
  GND: Grove1.GND, Part2.GND, Part3.GND
  VCC: Grove1.VCC, Part2.VCC, Part3.+5V
  N1: Grove1.SDA, Part3.A_IN_4
  N2: Grove1.SCL, Part3.A_IN_5
  N3: Part2.DATA, Part3.DIG_1
